// Logisim project Ex11.circ as structural Verilog: 1 circuit, main circuit main
module main (
  input  [7:0] in_1,
  input  in_2,
  input  in_3,
  output [7:0] out_4
);

  wire clock_1_out;

  Clock clock_1 (.out(clock_1_out));
  Register register_1 (.D(in_1), .en(in_2), .Q(out_4), .clk(clock_1_out), .clr(in_3));
endmodule
