// Logisim project Ex21.circ as structural Verilog: 1 circuit, main circuit main
module main (
  input  in_1,
  input  in_2,
  input  in_3,
  input  in_4,
  output T_Q_Q_prime,
  output _1_0_1
);

  wire clock_1_out;

  Clock clock_1 (.out(clock_1_out));
  T_Flip_Flop t_ff_1 (
    .clk(clock_1_out), .T(in_1), .Q(T_Q_Q_prime), .Qn(_1_0_1), .preset(in_2), .reset(in_4), .en(in_3));

  // Notes on the sheet:
  //   0 0 0
  //   0 1 0
  //   1 1 0
endmodule
