// Logisim project Easy.circ as structural Verilog: 1 circuit, main circuit main
module main (
  input  in_1,
  input  in_2,
  input  in_3,
  input  in_4,
  input  in_5,
  input  in_6,
  input  in_7,
  input  in_8,
  input  in_9,
  input  in_10,
  input  in_11,
  input  in_12,
  input  in_13,
  input  in_14,
  input  in_15,
  input  in_16,
  input  in_17,
  input  Ex_4E,
  input  in_19,
  input  in_20,
  input  in_21,
  input  in_22,
  input  in_23,
  input  in_24,
  input  Ex_6E,
  input  in_26,
  input  in_27,
  input  in_28,
  input  in_29,
  input  in_30,
  input  in_31,
  input  sau,
  input  in_33,
  input  in_34,
  input  in_35,
  input  in_36,
  input  in_37,
  input  sau_2,
  input  in_39,
  input  in_40,
  input  in_41,
  input  in_42,
  input  in_43,
  input  in_44,
  input  in_45,
  input  in_46,
  input  in_47,
  input  in_48,
  input  in_49,
  input  in_50,
  input  in_51,
  input  in_52,
  input  in_53,
  input  in_54,
  input  in_55,
  input  in_56,
  input  in_57,
  input  in_58,
  input  in_59,
  input  in_60,
  input  in_61,
  input  in_62,
  input  in_63,
  input  in_64,
  input  in_65,
  output out_66,
  output out_67,
  output out_68,
  output out_69,
  output out_70,
  output out_71,
  output out_72,
  output out_73,
  output out_74,
  output [1:0] out_75,
  output out_76,
  output out_77,
  output out_78,
  output out_79,
  output out_80,
  output out_81,
  output out_82,
  output out_83,
  output out_84,
  output out_85,
  output out_86,
  output out_87,
  output out_88
);

  wire and_2_out, nand_1_out, nand_2_out, nand_3_out, nand_4_out, nand_5_out, nand_6_out, nand_7_out,
       nand_8_out, nand_9_out, nand_10_out, nand_11_out, nand_12_out, nand_18_out, nand_19_out, nand_20_out,
       nand_21_out, nand_22_out, nand_23_out, nand_24_out, nand_25_out, nor_1_out, nor_2_out, nor_3_out,
       nor_4_out, nor_6_out, nor_7_out, or_3_out, or_4_out, xnor_2_out, xnor_3_out, xnor_4_out, xor_2_out;

  nand nand_1 (nand_1_out, in_1, in_2);
  xor xor_1 (out_68, in_3, in_4);
  nor nor_1 (nor_1_out, in_6, in_10);
  xnor xnor_1 (out_71, in_11, in_12);
  and and_1 (out_72, in_13, in_15, in_16);
  or or_1 (out_74, Ex_4E, in_20, in_21, in_22);
  nor nor_2 (nor_2_out, Ex_6E, Ex_6E);
  nor nor_3 (nor_3_out, in_26, in_26);
  nor nor_4 (nor_4_out, in_27, in_28);
  xor xor_2 (xor_2_out, in_29, in_31);
  nand nand_2 (nand_2_out, in_35, in_35);
  nand nand_3 (nand_3_out, in_36, in_36);
  nand nand_4 (nand_4_out, in_39, in_39);
  nand nand_5 (nand_5_out, in_41, in_41);
  nand nand_6 (nand_6_out, in_43, in_44, in_45, in_46);
  or or_2 (out_83, in_47, in_48, in_49, in_50, in_51);
  nor nor_5 (out_84, in_52, in_52, in_52);
  ExactlyOne xor_3 (.out(out_85), .in0(in_53), .in1(in_55), .in3(in_56), .in4(in_58));
  NotExactlyOne xnor_2 (.out(xnor_2_out), .in0(in_59), .in1(in_60), .in3(in_61), .in4(in_62));
  xnor xnor_3 (xnor_3_out, in_63, in_64);
  xnor xnor_4 (xnor_4_out, in_63, in_64);
  nand nand_7 (nand_7_out, in_1, nand_1_out);
  nand nand_8 (nand_8_out, nand_1_out, in_2);
  nor nor_6 (nor_6_out, in_6, nor_1_out);
  nor nor_7 (nor_7_out, nor_1_out, in_10);
  nor nor_8 (out_76, nor_2_out, nor_3_out);
  nor nor_9 (out_77, nor_4_out, nor_4_out);
  xor xor_4 (out_78, xor_2_out, in_33);
  nand nand_9 (nand_9_out, in_35, in_36);
  nand nand_10 (nand_10_out, nand_2_out, nand_3_out);
  nand nand_11 (nand_11_out, in_39, in_41);
  nand nand_12 (nand_12_out, nand_4_out, nand_5_out);
  nand nand_13 (out_82, nand_6_out, nand_6_out, nand_6_out, nand_6_out);
  nand nand_14 (out_67, nand_7_out, nand_8_out);
  nor nor_10 (out_70, nor_6_out, nor_7_out);
  xor xor_5 (out_86, in_54, in_57);
  NotExactlyOne xnor_5 (.out(out_87), .in0(xnor_2_out), .in1(xnor_2_out), .in3(xnor_2_out), .in4(xnor_2_out));
  NotExactlyOne xnor_6 (.out(out_88), .in0(xnor_3_out), .in1(in_63), .in2(in_64), .in4(xnor_4_out));
  and and_2 (and_2_out, in_14, in_17);
  nand nand_15 (out_75[0], in_23, in_23);
  nand nand_16 (out_75[1], in_24, in_24);
  nand nand_17 (out_80, nand_9_out, nand_10_out, nand_11_out, nand_12_out);
  and and_3 (out_73, and_2_out, in_19);
  ExactlyOne xor_6 (.out(out_79), .in0(in_30), .in2(sau), .in4(in_34));
  nand nand_18 (nand_18_out, in_37, sau_2);
  nand nand_19 (nand_19_out, in_40, in_42);
  nand nand_20 (nand_20_out, in_37, nand_18_out);
  nand nand_21 (nand_21_out, nand_18_out, sau_2);
  nand nand_22 (nand_22_out, in_40, nand_19_out);
  nand nand_23 (nand_23_out, nand_19_out, in_42);
  or or_3 (or_3_out, in_5, in_7);
  or or_4 (or_4_out, in_8, in_9);
  nand nand_24 (nand_24_out, nand_20_out, nand_21_out);
  nand nand_25 (nand_25_out, nand_22_out, nand_23_out);
  or or_5 (out_69, or_3_out, or_4_out);
  nand nand_26 (out_81, nand_24_out, nand_24_out, nand_25_out, nand_25_out);

  // Notes on the sheet:
  //   Ex 1E
  //   Ex 2E
  //   Ex 3E
  //   Ex 7E
  //   Ex 8E
  //   Ex 9E
  //   Ex 10E
  //   Ex 11E
  //   Ex 12E
  //   ?
  //   Ex 5E
endmodule
