// Logisim project Hard.circ as structural Verilog: 1 circuit, main circuit main
module main (
  input  [7:0] in_1,
  input  [7:0] in_2,
  input  [7:0] in_3,
  input  [3:0] in_4,
  input  [3:0] in_5,
  input  in_6,
  input  [3:0] in_7,
  input  Ex__4H,
  input  [7:0] in_9,
  input  [7:0] in_10,
  input  in_11,
  output [7:0] out_12,
  output [7:0] out_13,
  output [7:0] out_14,
  output out_15,
  output out_16
);

  wire decoder_1_out0, decoder_1_out1, decoder_1_out2, decoder_1_out3, decoder_1_out4, decoder_1_out5,
       decoder_1_out6, decoder_1_out7, decoder_1_out8, decoder_1_out9, decoder_1_out10, decoder_1_out11,
       decoder_1_out12, decoder_1_out13, decoder_1_out14, decoder_1_out15;

  Decoder #(.select(4)) decoder_1 (
    .out0(decoder_1_out0), .out1(decoder_1_out1), .out2(decoder_1_out2), .out3(decoder_1_out3),
    .out4(decoder_1_out4), .out5(decoder_1_out5), .out6(decoder_1_out6), .out7(decoder_1_out7),
    .out8(decoder_1_out8), .out9(decoder_1_out9), .out10(decoder_1_out10), .out11(decoder_1_out11),
    .out12(decoder_1_out12), .out13(decoder_1_out13), .out14(decoder_1_out14), .out15(decoder_1_out15),
    .sel(in_7), .en(in_6));
  LED led_1 (.in(decoder_1_out0));
  LED led_2 (.in(decoder_1_out1));
  LED led_3 (.in(decoder_1_out2));
  LED led_4 (.in(decoder_1_out3));
  LED led_5 (.in(decoder_1_out4));
  LED led_6 (.in(decoder_1_out5));
  LED led_7 (.in(decoder_1_out6));
  LED led_8 (.in(decoder_1_out7));
  LED led_9 (.in(decoder_1_out8));
  LED led_10 (.in(decoder_1_out9));
  LED led_11 (.in(decoder_1_out10));
  LED led_12 (.in(decoder_1_out11));
  LED led_13 (.in(decoder_1_out12));
  LED led_14 (.in(decoder_1_out13));
  LED led_15 (.in(decoder_1_out14));
  LED led_16 (.in(decoder_1_out15));
  Adder adder_1 (.a(in_9), .b(in_10), .out(out_14), .cin(Ex__4H), .cout(in_11));
  Hex_Digit_Display hex_digit_display_1 (.value(in_4));  // open: dp
  Hex_Digit_Display hex_digit_display_2 (.value(in_5));  // open: dp
  Divider divider_1 (.a(in_1), .b(in_2), .out(out_12));  // open: upper, rem
  Negator negator_1 (.in(in_3), .out(out_13));

  // Notes on the sheet:
  //   Ex. 2H
  //   Ex. 20H
  //   Ex. 6H
  //   Ex. 12H
endmodule
