// Logisim project Medium.circ as structural Verilog: 1 circuit, main circuit main
module main (
  input  Ex_1M,
  input  Ex_11M,
  input  Ex_2M,
  input  Ex_12M,
  input  in_5,
  input  in_6,
  input  Ex_13M,
  input  Ex_3M,
  input  in_9,
  input  in_10,
  input  Ex_4M,
  input  in_12,
  input  Ex_14M,
  input  in_14,
  input  Ex_15M,
  input  Ex_16M,
  input  Ex_6M,
  input  in_18,
  input  Ex_7M,
  input  in_20,
  input  in_21,
  input  Ex_17M,
  input  in_23,
  input  in_24,
  input  Ex_8M,
  input  Ex_18M,
  input  in_27,
  input  in_28,
  input  Ex_19M,
  input  Ex_9M,
  input  in_31,
  input  Ex_10M,
  input  in_33,
  input  in_34
);

  wire and_1_out, and_2_out, and_3_out, nand_1_out, nand_2_out, nor_1_out, not_1_out, not_2_out, or_1_out,
       or_2_out, or_3_out, xnor_1_out, xnor_2_out, xnor_3_out, xnor_4_out, xor_1_out, xor_2_out, xor_3_out,
       xor_4_out;

  not not_1 (not_1_out, Ex_8M);
  not not_2 (not_2_out, Ex_9M);
  xnor xnor_1 (xnor_1_out, Ex_1M, Ex_2M);
  LED led_1 (.in(xnor_1_out));
  or or_1 (or_1_out, in_6, Ex_3M);
  LED led_2 (.in(or_1_out));
  xor xor_1 (xor_1_out, in_9, Ex_4M);
  LED led_3 (.in(xor_1_out));
  xor xor_2 (xor_2_out, 1'b1, 1'b0);
  LED led_4 (.in(xor_2_out));
  LED led_5 (.in(xor_3_out));
  xor xor_3 (xor_3_out, 1'b0, 1'b1);
  LED led_6 (.in(nor_1_out));
  nor nor_1 (nor_1_out, Ex_6M, Ex_7M);
  and and_1 (and_1_out, in_21, in_23);
  LED led_7 (.in(and_1_out));
  LED led_8 (.in(xor_4_out));
  xor xor_4 (xor_4_out, not_1_out, in_27);
  LED led_9 (.in(not_2_out));
  LED led_10 (.in(Ex_10M));
  and and_2 (and_2_out, Ex_11M, Ex_12M);
  or or_2 (or_2_out, in_5, Ex_13M);
  nand nand_1 (nand_1_out, in_10, in_12);
  xnor xnor_2 (xnor_2_out, Ex_14M, in_14);
  or or_3 (or_3_out, Ex_15M, Ex_16M);
  xnor xnor_3 (xnor_3_out, in_18, in_20);
  nand nand_2 (nand_2_out, Ex_17M, in_24);
  xnor xnor_4 (xnor_4_out, Ex_18M, in_28);
  and and_3 (and_3_out, Ex_19M, in_31);
  LED led_11 (.in(and_2_out));
  LED led_12 (.in(or_2_out));
  LED led_13 (.in(nand_1_out));
  LED led_14 (.in(xnor_2_out));
  LED led_15 (.in(or_3_out));
  LED led_16 (.in(xnor_3_out));
  LED led_17 (.in(nand_2_out));
  LED led_18 (.in(xnor_4_out));
  LED led_19 (.in(and_3_out));

  // Notes on the sheet:
  //   Ex 5M
endmodule
